# Fritzing sketch Aeroponics (saved by Fritzing 0.9.4)
breadboards: 1

parts:
  Part1 = Arduino Mega 2560 (Rev3)
  VCC2 = Battery block 9V
  M2 = RioRand LM2596
  DS1 = DS18B20 1-Wire Temperature Sensor [part_number=DS18B20]
  R1 = Resistor [tolerance=±5% resistance=220 package=THT]
  KY-5 = Keyes Relay [package=THT]
  KY-6 = Keyes Relay [package=THT]
  WATER_PUMP2 = water pump/motor
  WATER_PUMP3 = water pump/motor
  KY-7 = Keyes Relay [package=THT]
  F1 = Fan - Ventilador [package=THT]
  GSM_SIM_GPSR_SMS_SIM900_SIM1 = SIM800L [package=THT]
  LCD1 = LCD screen  # not connected
  LCM1602_IIC2 = LCM1602 IIC [part_number="LCM1602 IIC" chip_label="LCM1602 IIC" package="DIP (Dual Inline) [THT]"]
  KY-8 = Keyes Relay [package=THT]
  KY-9 = Keyes Relay [package=THT]
  KY-10 = Keyes Relay [package=THT]
  WATER_PUMP4 = water pump/motor
  WATER_PUMP5 = water pump/motor
  WATER_PUMP6 = water pump/motor
  RHT1 = Humidity and Temperature Sensor RHT03
  Load_Cell1 = Load Cell - Red/white/black/green
  Part2 = HX711 Weighing Sensor Module

nets:
  N1: Part1.D21/SCL, LCM1602_IIC2.SCL
  N2: Part1.D20/SDA, LCM1602_IIC2.SDA
  N3: Part1.D19/RX1, GSM_SIM_GPSR_SMS_SIM900_SIM1.SIM_TXD
  N4: Part1.D18/TX1, GSM_SIM_GPSR_SMS_SIM900_SIM1.SIM_RXD
  N5: Part1.D12_PWM, KY-10.signal
  N6: Part1.D11_PWM, KY-9.signal
  N7: Part1.D10_PWM, KY-8.signal
  N8: Part1.D9_PWM, KY-6.signal
  N9: Part1.D8_PWM, KY-5.signal
  5V: Part1.5V, Part2.VCC
  GND: Part1.GND, M2.Pin_4, DS1.GND, KY-5.ground, KY-6.ground, KY-7.ground, GSM_SIM_GPSR_SMS_SIM900_SIM1.GND, LCM1602_IIC2.GND, KY-8.ground, KY-9.ground, KY-10.ground, RHT1.GND_2, Part2.GND
  VCC: Part1.VIN, M2.Pin_3, KY-5.power, KY-6.power, KY-7.power, GSM_SIM_GPSR_SMS_SIM900_SIM1.5V, LCM1602_IIC2.VCC, KY-8.power, KY-9.power, KY-10.power, RHT1.Vcc
  N10: Part1.D2_PWM, RHT1.Data-signal
  N11: Part1.D3_PWM, R1.Pin_1
  N12: Part1.D5_PWM, Part2.CK/TX
  N13: Part1.D6_PWM, Part2.DO/RX
  N14: Part1.D7_PWM, KY-7.signal
  N15: VCC2.-, M2.Pin_2, WATER_PUMP2.pin_1, WATER_PUMP3.pin_1, F1.GND, WATER_PUMP4.pin_1, WATER_PUMP5.pin_1, WATER_PUMP6.pin_1
  N16: VCC2.+, M2.Pin_1, KY-5.NO, KY-6.NO, KY-7.NO, KY-8.NO, KY-9.NO, KY-10.NO
  N17: DS1.DQ, DS1.VDD, R1.Pin_0
  N18: KY-5.C, WATER_PUMP2.pin_2
  N19: KY-6.C, WATER_PUMP3.pin_2
  N20: KY-7.C, F1.5V
  N21: KY-8.C, WATER_PUMP4.pin_2
  N22: KY-9.C, WATER_PUMP5.pin_2
  N23: KY-10.C, WATER_PUMP6.pin_2
  N24: Load_Cell1.wire1, Part2.E+
  N25: Load_Cell1.wire2, Part2.A+
  N26: Load_Cell1.wire3, Part2.E-
  N27: Load_Cell1.wire4, Part2.A-

notes:
  12V
  5v
  Submersible Pump (Humidity)
  Submersible Pump (Watering)
  Peristaltic Pump (Water)
  Peristaltic Pump (Solution A)
  Peristaltic Pump (Solution B)

custom parts:
  Keyes Relay: The Keyes 5V relay module is suitable for SCM development, home appliance control. It uses a 5V~12V TIL control signal which can control DC / AC signal.
  water pump/motor: WATER PUMP BY ARDUBLOCKTR
  Fan - Ventilador: Ventilador de 2 pines, se encuentra comunmente en computadoras de escritorio
  LCM1602 IIC: I2C-Module to use a 1602 or 2004 LCD on with the wire.h libory Serial LCD Modul
  Load Cell - Red/white/black/green: A rectangle load cell/weighting pressure Sensor with four wires - Red, white, black, green. Normally corresponding with E+, E-, A+, A- respectively.
  HX711 Weighing Sensor Module: HX711 is a precision 24-bit analog-to-digital converter (ADC) designed for weigh scales and industrial control applications to interface directly with a bridge sensor.

// code stored in the sketch: LED Test.ino
#define LED 13

void setup() {
	pinMode(LED, OUTPUT);
}

void loop {
	digitalWrite(LED,  HIGH);
	delay(1000);
	digitalWrite(LED, LOW);
	delay(1000);
}
